// Logisim project CPU_8bits.circ as structural Verilog: 4 circuits, main circuit main
module main (
);

  wire undriven;
  wire [3:0] undriven_3;
  wire [7:0] alu_8bit_xmx077_1_out_4, AR1_out_5, bit_extender_1_out, controlled_buffer_1_out,
       controlled_buffer_3_out, DR1_out_5, DR2_out_5, dr_1_out_5, ER_out_5, IR_out_5, main_1_a_out,
       main_1_b_out, main_5_pc_out, multiplexer_1_out, pc_add_1_s_out, R4_out_5, rom_1_data, undriven_2;

  DR DR2 (.in_1(main_1_a_out), .out_5(DR2_out_5));  // open: LDDR, CLK, CLEAR
  ALU_8bit_xmx077 alu_8bit_xmx077_1 (
    .A(DR2_out_5), .B(DR1_out_5), .out_4(alu_8bit_xmx077_1_out_4));  // open: in_3, out_5, out_6, out_7
  RF_4_main main_1 (
    .D_in(ER_out_5), .A_out(main_1_a_out), .B_out(main_1_b_out));  // open: clk, RS, RD, reset, Write, WRD, R1_o, R0_o, R3_o, R2_o
  DR ER (.in_1(controlled_buffer_1_out), .out_5(ER_out_5));  // open: LDDR, CLK, CLEAR
  Controlled_Buffer #(.width(8)) controlled_buffer_1 (
    .in(alu_8bit_xmx077_1_out_4), .out(controlled_buffer_1_out));  // open: en
  DR DR1 (.in_1(main_1_b_out), .out_5(DR1_out_5));  // open: LDDR, CLK, CLEAR
  Controlled_Buffer #(.width(8)) controlled_buffer_2 (.in(main_1_b_out), .out(controlled_buffer_1_out));  // open: en
  // Timing_sequence_main main_2: pin names not known
  RAM_8bits_main main_3 (
    .Add_in(AR1_out_5), .D_in(controlled_buffer_3_out), .D_out(controlled_buffer_1_out), .CLR(undriven));  // open: Write, cs, clk, Read
  Controlled_Buffer #(.width(8)) controlled_buffer_3 (
    .in(controlled_buffer_1_out), .out(controlled_buffer_3_out));  // open: en
  DR AR1 (.in_1(controlled_buffer_1_out), .out_5(AR1_out_5), .CLEAR(undriven));  // open: LDDR, CLK
  // uAddressR_main main_4: pin names not known
  DR dr_1 (.in_1(main_5_pc_out), .out_5(dr_1_out_5));  // open: LDDR, CLK, CLEAR
  PC_Register3_main main_5 (
    .PC_in(pc_add_1_s_out), .Preset_data(undriven_2), .PC_out(main_5_pc_out));  // open: clk_T4, reset, PC_1, LDPC
  PC_ADD pc_add_1 (.Din_1(R4_out_5), .Din_2(main_5_pc_out), .S_out(pc_add_1_s_out));  // open: PC_ADD
  DR R4 (.in_1(multiplexer_1_out), .out_5(R4_out_5));  // open: LDDR, CLK, CLEAR
  Multiplexer #(.width(8), .enable("false")) multiplexer_1 (
    .in0(controlled_buffer_1_out), .in1(bit_extender_1_out), .out(multiplexer_1_out));  // open: sel
  ROM rom_1 (.addr(dr_1_out_5), .data(rom_1_data));  // open: sel
  assign bit_extender_1_out = {{4{1'b0}}, undriven_3};  // Bit_Extender bit_extender_1
  DR IR (.in_1(rom_1_data), .out_5(IR_out_5));  // open: LDDR, CLK, CLEAR
endmodule

module DR (
  input  [7:0] in_1,
  input  LDDR,
  input  CLK,
  input  CLEAR,
  output [7:0] out_5
);

  Register register_1 (.D(in_1), .en(LDDR), .Q(out_5), .clk(CLK), .clr(CLEAR));
endmodule

module PC_ADD (
  input  [7:0] Din_1,
  input  [7:0] Din_2,
  input  PC_ADD,
  output [7:0] S_out
);

  wire [7:0] fa_8bits_unsigned_xmx077_1_s_a;

  FA_8bits_unsigned_xmx077 fa_8bits_unsigned_xmx077_1 (
    .A(Din_1), .B(Din_2), .S_A(fa_8bits_unsigned_xmx077_1_s_a));  // open: out_4, out_5
  Multiplexer #(.width(8), .enable("false")) multiplexer_1 (
    .in0(Din_1), .in1(fa_8bits_unsigned_xmx077_1_s_a), .out(S_out), .sel(PC_ADD));
endmodule

module uC (
  input  [5:0] in_1,
  output [21:0] uOP_signal
);

  wire CF, nor_1_out, not_1_out, not_2_out, P3, R0, undriven, undriven_2, ZF;
  wire [8:0] register_1_q;
  wire [31:0] rom_1_data;

  ROM #(.addrWidth(6), .dataWidth(32)) rom_1 (.addr(in_1), .data(rom_1_data), .sel(1'b1));
  Register #(.width(32)) register_1 (
    .D(rom_1_data), .en(1'b1), .Q({uOP_signal, P3, register_1_q[8:7], R0, register_1_q[5:0]}),
    .clk(undriven_2), .clr(undriven));
  not not_1 (not_1_out, ZF);
  nor nor_1 (nor_1_out, P3, register_1_q[7]);
  not not_2 (not_2_out, register_1_q[8]);
  // AND_Gate and_1 has open pins: in0=not_1_out, in1=P3, out=open
  // AND_Gate and_2 has open pins: in0=CF, in1=R0, out=open
  // AND_Gate and_3 has open pins: in0=nor_1_out, in1=register_1_q[5], out=open
  // AND_Gate and_4 is placed but not wired
  // AND_Gate and_5 has open pins: in0=not_2_out, out=open
  // AND_Gate and_6 is placed but not wired
  // AND_Gate and_7 is placed but not wired
  // AND_Gate and_8 is placed but not wired
  // AND_Gate and_9 is placed but not wired
  // AND_Gate and_10 is placed but not wired
  // AND_Gate and_11 is placed but not wired
  // AND_Gate and_12 is placed but not wired
endmodule
